// Logisim project lab02-1.circ as structural Verilog: 1 circuit, main circuit main
module main (
  input  A,
  input  B,
  input  C,
  input  D,
  output S1,
  output S2,
  output S3,
  output S4,
  output S5,
  output S6,
  output S7
);

  wire and_1_out, and_2_out, and_3_out, and_4_out, and_5_out, and_6_out, and_7_out, and_8_out, and_9_out,
       and_10_out, not_1_out, xnor_1_out, xnor_2_out, xor_1_out;

  xnor xnor_1 (xnor_1_out, B, D);
  xnor xnor_2 (xnor_2_out, C, D);
  not not_1 (not_1_out, B);
  or or_1 (S3, ~C, B, D);  // OR_Gate
  and and_1 (and_1_out, ~B, ~D);  // AND_Gate
  and and_2 (and_2_out, C, ~B);  // AND_Gate
  and and_3 (and_3_out, C, ~D);  // AND_Gate
  and and_4 (and_4_out, B, ~C, D);  // AND_Gate
  and and_5 (and_5_out, ~B, ~D);  // AND_Gate
  and and_6 (and_6_out, C, ~D);  // AND_Gate
  and and_7 (and_7_out, ~C, ~D);  // AND_Gate
  and and_8 (and_8_out, ~C, B);  // AND_Gate
  and and_9 (and_9_out, B, ~D);  // AND_Gate
  xor xor_1 (xor_1_out, B, C);
  and and_10 (and_10_out, C, ~D);  // AND_Gate
  or or_2 (S1, xnor_1_out, A, C);
  or or_3 (S2, xnor_2_out, not_1_out);
  or or_4 (S4, and_1_out, and_2_out, and_3_out, and_4_out, A);
  or or_5 (S5, and_5_out, and_6_out);
  or or_6 (S6, and_7_out, and_8_out, and_9_out, A);
  or or_7 (S7, xor_1_out, and_10_out, A);
endmodule
